# Fritzing sketch Preamp Bajo (saved by Fritzing 0.9.3b)
circuit board: 3.59109cm x 2.99061cm
breadboards: 1

parts:
  J1 = female pin header, 2 pins [form="♀ (female)"]
  C4 = Electrolytic Capacitor [capacitance=1µF voltage=20V package="100 mil [THT, electrolytic]"]
  C12 = Electrolytic Capacitor [capacitance=1µF package="100 mil [THT, electrolytic]"]
  J2 = female pin header, 1 pin [form="♀ (female)"]
  R11 = Resistor [tolerance=±5% resistance=220 package="1206 [SMD]"]
  R1 = Resistor [tolerance=±5% resistance=130k package="1206 [SMD]"]
  R8 = Resistor [tolerance=±5% resistance=220 package="1206 [SMD]"]
  R13 = Resistor [tolerance=±5% resistance=220 package="1206 [SMD]"]
  R15 = Resistor [tolerance=±5% resistance=220 package="1206 [SMD]"]
  R14 = Resistor [tolerance=±5% resistance=220 package="1206 [SMD]"]
  R7 = Resistor [tolerance=±5% resistance=220 package="1206 [SMD]"]
  R6 = Trimmer Potentiometer [maximum_resistance=10kΩ package=THT]
  R10 = Trimmer Potentiometer [maximum_resistance=10kΩ package=THT]
  R9 = Trimmer Potentiometer [maximum_resistance=10kΩ package=THT]
  C11 = Ceramic Capacitor [capacitance=100nF package="200 mil [THT, multilayer]"]
  C10 = Ceramic Capacitor [capacitance=100nF package="200 mil [THT, multilayer]"]
  C7 = Ceramic Capacitor [capacitance=0.1nF package="200 mil [THT, multilayer]"]
  C8 = Ceramic Capacitor [capacitance=100nF package="200 mil [THT, multilayer]"]
  C9 = Ceramic Capacitor [capacitance=100nF package="200 mil [THT, multilayer]"]
  C6 = Ceramic Capacitor [capacitance=100nF package="200 mil [THT, multilayer]"]
  C3 = Ceramic Capacitor [capacitance=100nF package="200 mil [THT, multilayer]"]
  IC2 = SO08-EIAJ [chip_label=IC package=SO]
  R12 = Resistor [tolerance=±5% resistance=220 package="1206 [SMD]"]
  R3 = Resistor [tolerance=±5% resistance=10k package="1206 [SMD]"]
  R5 = Resistor [tolerance=±5% resistance=2.2M package="1206 [SMD]"]
  R4 = Resistor [tolerance=±5% resistance=2.2M package="1206 [SMD]"]
  C2 = Ceramic Capacitor [capacitance=100nF package="200 mil [THT, multilayer]"]
  C1 = Ceramic Capacitor [capacitance=8.2nF package="200 mil [THT, multilayer]"]
  R2 = Resistor [tolerance=±5% resistance=500k package="1206 [SMD]"]
  R16 = Resistor [tolerance=±5% resistance=220 package="1206 [SMD]"]
  C5 = Electrolytic Capacitor [capacitance=1µF voltage=20V package="100 mil [THT, electrolytic]"]
  J3 = female pin header, 1 pin [form="♀ (female)"]

nets:
  N1: J1.pin1, C2.1, C1.1
  GND/VSS: J1.pin2, C4.-, IC2.4, R5.Pin_0, C1.0, C5.-
  +2/Vb: C4.+, IC2.5, R5.Pin_1, R4.Pin_0, R2.Pin_1
  N2: C12.-, J2.pin1
  N3: C12.+, R16.Pin_1
  N4: R11.Pin_0, R9.leg1, C10.0
  O2: R11.Pin_1, R6.leg1, C7.0, IC2.7, R12.Pin_1, R16.Pin_0
  N5: R1.Pin_0, C3.1, C2.0
  -I1/O1: R1.Pin_1, R8.Pin_0, R15.Pin_0, R6.leg2, IC2.1, IC2.2
  N6: R8.Pin_1, R9.leg2, C10.1
  N7: R13.Pin_0, C9.0
  -2: R13.Pin_1, R14.Pin_1, R7.Pin_1, C7.1, IC2.6
  N8: R15.Pin_1, R10.leg2, C11.1
  N9: R14.Pin_0, C8.0
  N10: R7.Pin_0, C6.0
  N11: R6.wiper, C6.1
  N12: R10.leg1, C11.0, R12.Pin_0
  N13: R10.wiper, C9.1
  N14: R9.wiper, C8.1
  N15: C3.0, R3.Pin_0, R2.Pin_0
  +I1: IC2.3, R3.Pin_1
  9V/VDD: IC2.8, R4.Pin_1, C5.+, J3.pin1
