# Fritzing sketch Electret Mod (saved by Fritzing 0.9.10b)
circuit board: 2.21443cm x 1.04966cm
breadboards: 1

parts:
  R3 = Resistor [tolerance=±20% resistance=220 power=0.25 package="1206 [SMD]"]
  R2 = Resistor [tolerance=±20% resistance=220 power=0.25 package="1206 [SMD]"]
  C2 = Tantalum Capacitor [capacitance=1μF voltage=35V package="B 3528 [SMD, tantalum]"]
  C1 = Tantalum Capacitor [capacitance=1μF voltage=35V package="B 3528 [SMD, tantalum]"]
  R1 = Resistor [tolerance=±20% resistance=220 power=0.25 package="1206 [SMD]"]
  Mic = Pad [width=4.200590437808729 height=4.381402533991965 connect=center]
  GND = Pad [width=4.200590437808729 height=4.381402533991965 connect=center]
  GND_2 = Pad [width=2.9017010812932145 height=3.2 connect=center]
  S = Pad [width=2.9 height=3.2 connect=center]
  D = Pad [width=2.9 height=3.2 connect=center]
  J1 = female pin header, 3 pins [form="♀ (female)"]

nets:
  N1: R3.Pin_0, C2.-, C1.-, GND.pad, GND_2.pad
  N2: R3.Pin_1, S.pad
  N3: R2.Pin_0, C2.+
  N4: R2.Pin_1, J1.pin3
  N5: C1.+, R1.Pin_0
  N6: R1.Pin_1, J1.pin1
  N7: Mic.pad, D.pad, J1.pin2
