# Fritzing sketch FCBUSB (saved by Fritzing 0.9.3b)
circuit board: 1.94466cm x 3.50268cm
breadboards: 1

parts:
  Componente2 = Arduino Pro Micro (Clone)
  IC1 = IC, DIP package, 8 pins [chip_label=IC]
  D2 = Diode [package=diode-1n4148]
  R1 = Resistor [tolerance=±5% resistance=220 package=THT]
  R2 = Resistor [tolerance=±5% resistance=10k package=THT]
  J1 = female pin header, 10 pins [form="♀ (female)"]

nets:
  N1: Componente2.RXI, IC1.pin6, R2.Pin_1
  N2: Componente2.GND, IC1.pin5, J1.pin2
  N3: Componente2.D2, J1.pin3
  N4: Componente2.D3, J1.pin4
  N5: Componente2.D4, J1.pin5
  N6: Componente2.D5, J1.pin6
  N7: Componente2.D6, J1.pin7
  N8: Componente2.D7, J1.pin8
  N9: Componente2.D8, J1.pin9
  N10: Componente2.D9, J1.pin10
  N11: Componente2.VCC, IC1.pin8, R2.Pin_0, J1.pin1
  N12: IC1.pin2, D2.C, R1.Pin_0
  N13: IC1.pin3, D2.A
