# Fritzing sketch Main (saved by Fritzing 0.9.10b)
circuit board: 6.88566cm x 5.36311cm
breadboards: 1

parts:
  Componente1 = Arduino Uno (Rev3)
  XTAL1 = Crystal [frequency="16 Mhz" package=THT]
  C1 = Ceramic Capacitor [capacitance=100nF voltage=35V package="100 mil [THT, multilayer]"]
  C2 = Ceramic Capacitor [capacitance=100nF voltage=35V package="100 mil [THT, multilayer]"]
  J1 = double row female pin header, 6 pins [form="♀ (female)"]
  J2 = female pin header, 16 pins [form="♀ (female)"]
  J4 = Generic female header - 16 pins [form="♀ (female)" package=THT]
  LED1 = smd LED [color="Red (633nm)" current=0.030 package="0805 [SMD]"]
  LED3 = smd LED [color="Red (633nm)" current=0.030 package="0805 [SMD]"]
  LED2 = smd LED [color="Red (633nm)" current=0.030 package="0805 [SMD]"]
  R1 = Resistor [tolerance=±5% resistance=220 power=0.25 package="1206 [SMD]"]
  R2 = Resistor [tolerance=±5% resistance=220 power=0.25 package="1206 [SMD]"]
  R3 = Resistor [tolerance=±5% resistance=220 power=0.25 package="1206 [SMD]"]

nets:
  N1: Componente1.D8, R2.Pin_1
  N2: Componente1.D9_PWM, R3.Pin_1
  N3: Componente1.D10_PWM/SS, Componente1.D4, J1.pin3, J4.pin29
  N4: Componente1.D11_PWM/MOSI, J1.pin5, J2.pin15
  N5: Componente1.D12/MISO, J1.pin1, J2.pin16
  N6: Componente1.D13/SCK, J1.pin2, J4.pin16
  N7: Componente1.GND, J1.pin4, J2.pin3, J2.pin5
  N8: Componente1.D7, R1.Pin_1
  N9: Componente1.5V, J1.pin6, J2.pin4, J2.pin6, J4.pin20, J4.pin17
  N10: XTAL1.pin_0, C1.1
  N11: XTAL1.pin_1, C2.1, J2.pin7
  N12: C1.0, C2.0, J4.pin21
  N13: LED1.anode, R3.Pin_0
  N14: LED3.anode, R2.Pin_0
  N15: LED2.anode, R1.Pin_0

custom parts:
  Generic female header - 16 pins: Generic female header
