# Fritzing sketch Slave (saved by Fritzing 0.9.10b)
circuit board: 7.04149cm x 4.23182cm
breadboards: 1

parts:
  ATmega_328p = atmega328 [package=dip]
  ATmega_16/32 = ATmega644 [package=pdpi]
  ICSP = double row female pin header, 6 pins [form="♀ (female)"]
  8MHz = CRYSTAL [package=hc49u-v]
  16MHz = CRYSTAL [package=hc49u-v]
  J2 = female pin header, 3 pins [form="♀ (female)"]
  J3 = female pin header, 3 pins [form="♀ (female)"]
  C1 = Ceramic Capacitor [capacitance=100nF voltage=35V package="100 mil [THT, multilayer]"]
  C2 = Ceramic Capacitor [capacitance=100nF voltage=35V package="100 mil [THT, multilayer]"]

nets:
  N1: ATmega_328p.RESET, ATmega_16/32.RESET, ICSP.pin3
  VCC: ATmega_328p.VCC, ATmega_16/32.VCC, ICSP.pin6
  N2: ATmega_328p.GND#7, ATmega_16/32.GND#10
  N3: ATmega_328p.XLAT1, ATmega_16/32.XTAL1, J3.pin2, C2.0
  N4: ATmega_328p.XLAT2, ATmega_16/32.XTAL2, J2.pin2, C1.1
  N5: ATmega_328p.D11_(PWM), ATmega_16/32.PB5, ICSP.pin5
  N6: ATmega_328p.D12, ATmega_16/32.PB6, ICSP.pin1
  N7: ATmega_328p.D13, ATmega_16/32.PB7, ICSP.pin2
  N8: 8MHz.1, J2.pin1
  N9: 8MHz.2, J3.pin1
  N10: 16MHz.1, J2.pin3
  N11: 16MHz.2, J3.pin3
