# Fritzing sketch Buttons-nst (saved by Fritzing 0.9.3b)
circuit board: 2.90941cm x 4.6426cm
breadboards: 1

parts:
  Main_Connector = female pin header, 8 pins [form="♀ (female)"]
  5V = female pin header, 1 pin [form="♀ (female)"]
  B5 = female pin header, 1 pin [form="♀ (female)"]
  B2 = female pin header, 1 pin [form="♀ (female)"]
  B4 = female pin header, 1 pin [form="♀ (female)"]
  R8 = Resistor [tolerance=±5% resistance=220 package=THT]
  R12 = Resistor [tolerance=±5% resistance=220 package=THT]
  B6 = female pin header, 1 pin [form="♀ (female)"]
  R2 = Resistor [tolerance=±5% resistance=220 package=THT]
  B1 = female pin header, 1 pin [form="♀ (female)"]
  R10 = Resistor [tolerance=±5% resistance=220 package=THT]
  R4 = Resistor [tolerance=±5% resistance=220 package=THT]
  B3 = female pin header, 1 pin [form="♀ (female)"]
  R6 = Resistor [tolerance=±5% resistance=220 package=THT]

nets (from the pcb view):
  N1: Main_Connector.pin1, R2.Pin_1, B1.pin1
  N2: Main_Connector.pin2, B2.pin1, R4.Pin_1
  N3: Main_Connector.pin3, B3.pin1, R6.Pin_1
  N4: Main_Connector.pin4, B4.pin1, R8.Pin_1
  N5: Main_Connector.pin5, B5.pin1, R10.Pin_1
  N6: Main_Connector.pin6, R12.Pin_1, B6.pin1
  N7: Main_Connector.pin7, 5V.pin1
  N8: Main_Connector.pin8, R8.Pin_0, R12.Pin_0, R2.Pin_0, R10.Pin_0, R4.Pin_0, R6.Pin_0
