# Fritzing sketch Comunicación2.0 (saved by Fritzing 0.9.3b)
circuit board: 6.61812cm x 3.78177cm
breadboards: 1

parts:
  LED1_XB1 = LED - 3mm [color="Red (633nm)" package="3 mm [THT]"]
  LED5 = LED - 3mm [color="Red (633nm)" package="3 mm [THT]"]
  LED6 = LED - 3mm [color="Red (633nm)" package="3 mm [THT]"]
  LED7 = LED - 3mm [color="Red (633nm)" package="3 mm [THT]"]
  R23 = Resistor [tolerance=±5% resistance=220 package="1206 [SMD]"]
  U3 = XBEE-1 [package=xbee-silk]
  R24 = Resistor [tolerance=±5% resistance=220 package="1206 [SMD]"]
  Main_Connector = female pin header, 5 pins [form="♀ (female)"]
  R30 = Resistor [tolerance=±5% resistance=1k package=THT]
  R31 = Resistor [tolerance=±5% resistance=1k package=THT]
  R21 = Resistor [tolerance=±5% resistance=220 package="1206 [SMD]"]
  HC-05 = Generic female header - 6 pins [form="♀ (female)" package=THT]
  6N138 = IC, DIP package, 8 pins [chip_label=IC]
  1n4149 = Diode [package=diode-1n4148]
  Midi_In1 = female pin header, 2 pins [form="♀ (female)"]
  R34 = Resistor [tolerance=±5% resistance=220 package="1206 [SMD]"]
  R33 = Resistor [tolerance=±5% resistance=220 package="1206 [SMD]"]
  R22 = Resistor [tolerance=±5% resistance=220 package="1206 [SMD]"]

nets:
  GND: LED1_XB1.cathode, LED5.cathode, LED6.cathode, LED7.cathode, U3.GND, Main_Connector.pin5, HC-05.GND
  N1: LED1_XB1.anode, R24.Pin_0
  N2: LED5.anode, R21.Pin_0
  N3: LED6.anode, R22.Pin_0
  N4: LED7.anode, R23.Pin_1
  RX-3V3: R23.Pin_0, U3.DIN, R30.Pin_0, R31.Pin_0, HC-05.RX
  TX-3V3: U3.DOUT, HC-05.TX
  N5: U3.RSSI, R21.Pin_1
  N6: U3.DIO5, R24.Pin_1
  5V: Main_Connector.pin1, HC-05.5V, 6N138.pin8, R33.Pin_0
  3V3: Main_Connector.pin2
  TX-5V: Main_Connector.pin3, 6N138.pin6, R33.Pin_1, R22.Pin_1
  RX-5V: Main_Connector.pin4, R31.Pin_1
  ENABLE: HC-05.EN
  STATE: HC-05.STATE
  N7: 6N138.pin2, 1n4149.C, R34.Pin_1
  N8: 6N138.pin3, 1n4149.A, Midi_In1.pin2
  N9: Midi_In1.pin1, R34.Pin_0

notes:
  TX
  RX
  3V3
  5V
  GND
  Communication Board
  MIDIEXP

custom parts:
  Generic female header - 6 pins: Generic female header
