# Fritzing sketch Led Strips y Power Source (saved by Fritzing 0.9.3b)
circuit board: 5.88331cm x 3.78566cm
breadboards: 1

parts:
  LM7805 = Voltage Regulator - 5V [package="TO220 [THT]"]
  C1 = Electrolytic Capacitor [capacitance=1µF package="200 mil [THT, electrolytic]"]
  C2 = Electrolytic Capacitor [capacitance=1µF package="100 mil [THT, electrolytic]"]
  IRF520 = Basic FET P-Channel [package="TO220 [THT]"]
  IRF520_2 = Basic FET P-Channel [package="TO220 [THT]"]
  IN12V = screw terminal, 2 pins
  OUT_5V = screw terminal, 2 pins
  MICROCONTROLLER_INPUTS(5V) = female pin header, 3 pins [form="♀ (female)"]
  LED_STRIP_II_(12V) = screw terminal, 2 pins
  LED_STRIP_I_(12V) = screw terminal, 2 pins
  U1 = Voltage Regulator - 12V [package="TO220 [THT]"]

nets:
  N1: LM7805.input_voltage, C1.+, IN12V.pin1, U1.input_voltage
  GND: LM7805.GND, C1.-, C2.-, IRF520.source, IRF520_2.source, IN12V.pin2, OUT_5V.pin2, MICROCONTROLLER_INPUTS(5V).pin3, U1.GND
  N2: LM7805.output_voltage, OUT_5V.pin1
  N3: C2.+, LED_STRIP_II_(12V).pin1, LED_STRIP_I_(12V).pin1, U1.output_voltage
  N4: IRF520.gate, MICROCONTROLLER_INPUTS(5V).pin2
  N5: IRF520.drain, LED_STRIP_II_(12V).pin2
  N6: IRF520_2.gate, MICROCONTROLLER_INPUTS(5V).pin1
  N7: IRF520_2.drain, LED_STRIP_I_(12V).pin2

notes:
  V-REGS / LED STRIPS
  MIDIEXP
  LM7812

custom parts:
  Voltage Regulator - 12V: 12V DC Voltage Regulator
