# Fritzing sketch Main Board2 (saved by Fritzing 0.9.3b)
circuit board: 10.1776cm x 5.36194cm
breadboards: 1

parts:
  Componente1 = Arduino Mega 2560 (Rev3)
  I2C_LCD = female pin header, 4 pins [form="♀ (female)"]
  ULN2003_Leds = ULN2003A [package="DIP16 [THT]"]
  Pedal_Leds = female pin header, 8 pins [form="♀ (female)"]
  R12 = Resistor [tolerance=±5% resistance=2.2k package="1206 [SMD]"]
  R11 = Resistor [tolerance=±5% resistance=2.2k package="1206 [SMD]"]
  R10 = Resistor [tolerance=±5% resistance=2.2k package="1206 [SMD]"]
  R9 = Resistor [tolerance=±5% resistance=2.2k package="1206 [SMD]"]
  R8 = Resistor [tolerance=±5% resistance=2.2k package="1206 [SMD]"]
  R7 = Resistor [tolerance=±5% resistance=2.2k package="1206 [SMD]"]
  R6 = Resistor [tolerance=±5% resistance=2.2k package="1206 [SMD]"]
  Analog_Inputs = female pin header, 7 pins [form="♀ (female)"]
  Pedal_Inputs = female pin header, 8 pins [form="♀ (female)"]
  S1 = Pushbutton [package="[THT]"]
  1n4148 = Diode [package=diode-1n4148]
  R21 = Resistor [tolerance=±5% resistance=220 package="1206 [SMD]"]
  R22 = Resistor [tolerance=±5% resistance=220 package="1206 [SMD]"]
  Communications = female pin header, 5 pins [form="♀ (female)"]
  Midi_In = female pin header, 2 pins [form="♀ (female)"]
  J1 = female pin header, 3 pins [form="♀ (female)"]
  J2 = screw terminal, 2 pins
  Pad1 = Pad [width=2.9384087615686258 height=2.0587144583006576 connect=center]  # not connected
  6N137 = IC, DIP package, 8 pins [chip_label=IC]

nets:
  N1: Componente1.A0, Analog_Inputs.pin3
  N2: Componente1.A1, Analog_Inputs.pin4
  N3: Componente1.A2, Analog_Inputs.pin5
  N4: Componente1.A3, Analog_Inputs.pin6
  N5: Componente1.A4, Analog_Inputs.pin7
  N6: Componente1.D21/SCL, Componente1.SCL, I2C_LCD.pin4
  N7: Componente1.D20/SDA, Componente1.SDA, I2C_LCD.pin3
  N8: Componente1.D19/RX1, R21.Pin_1, 6N137.pin6
  GND: Componente1.GND, I2C_LCD.pin1, ULN2003_Leds.0V, Analog_Inputs.pin1, Pedal_Inputs.pin8, S1.Pin_3, S1.Pin_4, Communications.pin5, J1.pin3, J2.pin2, 6N137.pin5
  N9: Componente1.D8_PWM, ULN2003_Leds.In_7
  N10: Componente1.RESET, S1.Pin_1, S1.Pin_2
  3V3: Componente1.3V3, Communications.pin2
  5V: Componente1.5V, I2C_LCD.pin2, ULN2003_Leds.COM_-_Common, Pedal_Leds.pin1, Analog_Inputs.pin2, Pedal_Inputs.pin7, R21.Pin_0, Communications.pin1, 6N137.pin8
  N11: Componente1.VIN, J2.pin1
  N12: Componente1.D0_RX0, Communications.pin3
  N13: Componente1.D1_TX0, Communications.pin4
  N14: Componente1.D2_PWM, ULN2003_Leds.In_1
  N15: Componente1.D3_PWM, ULN2003_Leds.In_2
  N16: Componente1.D4_PWM, ULN2003_Leds.In_3
  N17: Componente1.D5_PWM, ULN2003_Leds.In_4
  N18: Componente1.D6_PWM, ULN2003_Leds.In_5
  N19: Componente1.D7_PWM, ULN2003_Leds.In_6
  N20: Componente1.D32, Pedal_Inputs.pin6
  N21: Componente1.D34, Pedal_Inputs.pin5
  N22: Componente1.D36, Pedal_Inputs.pin4
  N23: Componente1.D38, Pedal_Inputs.pin3
  N24: Componente1.D40, Pedal_Inputs.pin2
  N25: Componente1.D42, Pedal_Inputs.pin1
  N26: Componente1.D46, J1.pin1
  N27: Componente1.D48, J1.pin2
  N28: ULN2003_Leds.Out_7, R6.Pin_0
  N29: ULN2003_Leds.Out_6, R7.Pin_0
  N30: ULN2003_Leds.Out_5, R8.Pin_0
  N31: ULN2003_Leds.Out_4, R9.Pin_0
  N32: ULN2003_Leds.Out_3, R10.Pin_0
  N33: ULN2003_Leds.Out_2, R11.Pin_0
  N34: ULN2003_Leds.Out_1, R12.Pin_0
  N35: Pedal_Leds.pin2, R6.Pin_1
  N36: Pedal_Leds.pin3, R7.Pin_1
  N37: Pedal_Leds.pin4, R8.Pin_1
  N38: Pedal_Leds.pin5, R9.Pin_1
  N39: Pedal_Leds.pin6, R10.Pin_1
  N40: Pedal_Leds.pin7, R11.Pin_1
  N41: Pedal_Leds.pin8, R12.Pin_1
  N42: 1n4148.A, Midi_In.pin2, 6N137.pin3
  N43: 1n4148.C, R22.Pin_1, 6N137.pin2
  N44: R22.Pin_0, Midi_In.pin1

notes:
  MAIN BOARD
  MIDIEXP
